# Fritzing sketch ESP8266_LedDimmer (saved by Fritzing 1.0.5)

parts:
  WeMos_D1_Mini1 = WeMos D1 Mini
  5V_3A_power_supply = Camdenboss CTB0158-2 [part_number=CTB0158-2 package=THT]
  5V_Led_strip = Camdenboss CTB0158-2 [part_number=CTB0158-2 package=THT]
  IRLZ44N = Basic FET N-Channel [package="DPak [SMD]"]
  R1 = Resistor [tolerance=±5% resistance=150 package="0603 [SMD]"]
  R2 = Resistor [tolerance=±5% resistance=100k package="0603 [SMD]"]
  RE1 = Rotary Encoder [package=THT]
  R3 = Resistor [tolerance=±5% resistance=10k package="0603 [SMD]"]
  R4 = Resistor [tolerance=±5% resistance=10k package="0603 [SMD]"]
  R5 = Resistor [tolerance=±5% resistance=10k package="0603 [SMD]"]

nets:
  N1: WeMos_D1_Mini1.3V3, R3.Pin_1, R4.Pin_1, R5.Pin_1
  N2: WeMos_D1_Mini1.5V, 5V_3A_power_supply.pin2, 5V_Led_strip.pin1
  N3: WeMos_D1_Mini1.D2, R1.Pin_0
  N4: WeMos_D1_Mini1.D5, RE1.EncoderPinA, R5.Pin_0
  N5: WeMos_D1_Mini1.D6, RE1.EncoderPinB, R4.Pin_0
  N6: WeMos_D1_Mini1.D7, RE1.SwitchPinE, R3.Pin_0
  N7: WeMos_D1_Mini1.G, 5V_3A_power_supply.pin1, IRLZ44N.source, R2.Pin_1, RE1.EncoderPinC, RE1.SwitchrPinD
  N8: 5V_Led_strip.pin2, IRLZ44N.drain
  N9: IRLZ44N.Gate, R1.Pin_1, R2.Pin_0

custom parts:
  WeMos D1 Mini: The D1 mini is a mini wifi board based on ESP-8266EX.
  Rotary Encoder: Rotary Encoder from ALPSec11e with switch.
